// Logisim project a.circ as structural Verilog: 1 circuit, main circuit main
module main (
  input  A,
  input  B,
  input  C,
  output out_4
);

  wire n7408_1_p3;

  // _7408 7408_1: pin names not known; wires that end beside it: A, C, n7408_1_p3, 1'b0, 1'b1
  // _7432 7432_1: pin names not known; wires that end beside it: B, n7408_1_p3, out_4, 1'b0, 1'b1
endmodule
