// Logisim project problem2.circ as structural Verilog: 1 circuit, main circuit main
module main (
  input  A,
  input  B,
  input  C,
  input  D,
  input  E,
  output out_6
);

  wire n7404_1_p3, n7404_1_p5, n7404_1_p7, n7408_1_p3, n7408_1_p6, n7408_1_p11;

  // _7404 7404_1: pin names not known; wires that end beside it: E, C, n7404_1_p3, A, n7404_1_p5, D, n7404_1_p7, 1'b0, 1'b1
  // _7408 7408_1: pin names not known; wires that end beside it: A, n7404_1_p3, n7408_1_p3, n7404_1_p5, C, n7408_1_p6, 1'b0, 1'b1, n7408_1_p6, n7404_1_p7, n7408_1_p11
  // _7432 7432_1: pin names not known; wires that end beside it: n7408_1_p3, n7408_1_p11, out_6, 1'b0, 1'b1
endmodule
