// Logisim project OneBitFullSubtractor.circ as structural Verilog: 1 circuit, main circuit main
module main (
  input  P,
  input  Q,
  input  R,
  output D,
  output B
);

  wire n7404_1_p3, n7404_1_p5, n7408_1_p4, n7408_1_p7, n7486_1_p3;

  // _7486 7486_1: pin names not known; wires that end beside it: P, Q, n7486_1_p3, n7486_1_p3, R, D, 1'b1
  // _7404 7404_1: pin names not known; wires that end beside it: 1'b0, n7486_1_p3, n7404_1_p3, P, n7404_1_p5, 1'b1
  // _7408 7408_1: pin names not known; wires that end beside it: 1'b0, R, n7404_1_p3, n7408_1_p4, n7404_1_p5, Q, n7408_1_p7, 1'b0, 1'b1
  // _7432 7432_1: pin names not known; wires that end beside it: n7408_1_p4, n7408_1_p7, B, 1'b0, 1'b1
endmodule
