// Logisim project 2105044.circ as structural Verilog: 1 circuit, main circuit main
module main (
  input  B,
  input  A,
  input  C,
  input  D,
  output out_5
);

  wire n7404_1_p2, n7432_1_p4;

  // _7404 7404_1: pin names not known; wires that end beside it: D, n7404_1_p2, 1'b0, 1'b1
  // _7432 7432_1: pin names not known; wires that end beside it: B, n7404_1_p2, C, n7432_1_p4, 1'b0, 1'b1, n7432_1_p4, A, out_5
endmodule
