// Logisim project problem1.circ as structural Verilog: 1 circuit, main circuit main
module main (
  input  A,
  input  B,
  input  C,
  input  D,
  input  E,
  output out_6
);

  wire n7404_1_p2, n7404_1_p4, n7404_1_p6, n7408_1_p3, n7408_1_p6, n7408_1_p11, n7408_1_p14, n7432_1_p3;

  // _7404 7404_1: pin names not known; wires that end beside it: E, n7404_1_p2, A, n7404_1_p4, B, n7404_1_p6, 1'b0, 1'b1
  // _7408 7408_1: pin names not known; wires that end beside it: n7404_1_p4, B, n7408_1_p3, n7408_1_p3, D, n7408_1_p6, 1'b0, 1'b1, A, n7404_1_p6, n7408_1_p11, n7408_1_p11, D, n7408_1_p14
  // _7432 7432_1: pin names not known; wires that end beside it: n7404_1_p2, n7408_1_p6, n7432_1_p3, n7432_1_p3, n7408_1_p14, out_6, 1'b0, 1'b1
endmodule
