// Logisim project 2105044.circ as structural Verilog: 1 circuit, main circuit main
module main (
  input  A4,
  input  A3,
  input  A2,
  input  A1,
  input  B4,
  input  B3,
  input  B2,
  input  B1,
  input  LSBin,
  input  MSBin,
  output o5,
  output o4,
  output o3,
  output o2,
  output o1
);

  wire xor_1_out, xor_2_out, xor_3_out, xor_4_out;

  xor xor_1 (xor_1_out, MSBin, B4);
  xor xor_2 (xor_2_out, MSBin, B3);
  xor xor_3 (xor_3_out, MSBin, B2);
  xor xor_4 (xor_4_out, MSBin, B1);
  _7483_main main_1 (
    ._1__A4(A4), ._2__S3(o3), ._3__A3(A3), ._4__B3(xor_2_out), ._5__Vcc(1'b1), ._6__S2(o2),
    ._7__B2(xor_3_out), ._8__A2(A2), ._16__B4(xor_1_out), ._15__S4(o4), .cout(o5), ._13__Cin(LSBin),
    ._12__GND(1'b0), ._11__B1(xor_4_out), ._10__A1(A1), ._9__S1(o1));
endmodule
